// Logisim project didar_kozhikov_lab01_mux.circ as structural Verilog: 1 circuit, main circuit main
module main (
  input  Sel,
  input  In1,
  input  In2,
  output Out1
);

  wire and_1_out, and_2_out;

  not not_1 (Sel, Sel);
  not not_2 (Sel, Sel);
  and and_1 (and_1_out, Sel, In1);
  and and_2 (and_2_out, Sel, In2);
  or or_1 (Out1, and_1_out, and_2_out);
endmodule
